# Fritzing sketch mm5450_multiplex (saved by Fritzing 0.9.3b)
breadboards: 3

parts:
  IC1 = IC, DIP package, 40 pins [chip_label=MM5450]
  C1 = Ceramic Capacitor [capacitance=1nF package="100 mil [THT, multilayer]"]
  R1 = Trimmer Potentiometer [maximum_resistance=0.1MΩ package=THT]
  Q1 = PNP-Transistor [package="TO92 [THT]"]
  R2 = Resistor [tolerance=±5% resistance=1k package=THT]
  R3 = Resistor [tolerance=±5% resistance=10k package=THT]
  LED1 = LED - 3mm [color="Red (633nm)" package="3 mm [THT]"]
  R4 = Resistor [tolerance=±5% resistance=1k package=THT]
  Q2 = PNP-Transistor [package="TO92 [THT]"]
  R5 = Resistor [tolerance=±5% resistance=10k package=THT]
  LED2 = LED - 3mm [color="Yellow (592nm)" package="3 mm [THT]"]
  Q3 = PNP-Transistor [package="TO92 [THT]"]
  R6 = Resistor [tolerance=±5% resistance=10k package=THT]
  R7 = Resistor [tolerance=±5% resistance=1k package=THT]
  LED3 = LED - 3mm [color="Green (565nm)" package="3 mm [THT]"]
  Part1 = Arduino Uno (Rev3)
  LED4 = LED - 3mm [color="Red (633nm)" package="3 mm [THT]"]
  LED5 = LED - 3mm [color="Red (633nm)" package="3 mm [THT]"]
  LED6 = LED - 3mm [color="Red (633nm)" package="3 mm [THT]"]
  LED7 = LED - 3mm [color="Red (633nm)" package="3 mm [THT]"]
  LED8 = LED - 3mm [color="Red (633nm)" package="3 mm [THT]"]
  LED9 = LED - 3mm [color="Red (633nm)" package="3 mm [THT]"]
  LED10 = LED - 3mm [color="Red (633nm)" package="3 mm [THT]"]
  LED11 = LED - 3mm [color="Red (633nm)" package="3 mm [THT]"]
  LED12 = LED - 3mm [color="Red (633nm)" package="3 mm [THT]"]
  LED13 = LED - 3mm [color="Red (633nm)" package="3 mm [THT]"]
  LED14 = LED - 3mm [color="Red (633nm)" package="3 mm [THT]"]
  LED15 = LED - 3mm [color="Red (633nm)" package="3 mm [THT]"]
  LED16 = LED - 3mm [color="Red (633nm)" package="3 mm [THT]"]
  LED17 = LED - 3mm [color="Red (633nm)" package="3 mm [THT]"]

nets:
  N1: IC1.pin1, C1.0, Part1.GND
  N2: IC1.pin19, C1.1, R1.wiper
  N3: IC1.pin20, R1.leg2, Q1.E, R3.Pin_0, Q2.E, R5.Pin_0, Q3.E, R6.Pin_0, Part1.5V
  N4: IC1.pin21, Part1.D13/SCK
  N5: IC1.pin22, Part1.D11_PWM/MOSI
  N6: IC1.pin23, Part1.D9_PWM
  N7: IC1.pin24, R2.Pin_0
  N8: IC1.pin25, R4.Pin_0
  N9: IC1.pin26, R7.Pin_0
  N10: IC1.pin27, LED1.cathode, LED2.cathode, LED3.cathode
  N11: IC1.pin28, LED17.cathode
  N12: IC1.pin29, LED16.cathode
  N13: IC1.pin30, LED15.cathode
  N14: IC1.pin31, LED14.cathode
  N15: IC1.pin32, LED13.cathode
  N16: IC1.pin33, LED12.cathode
  N17: IC1.pin34, LED10.cathode, LED11.cathode
  N18: IC1.pin35, LED9.cathode
  N19: IC1.pin36, LED8.cathode
  N20: IC1.pin37, LED7.cathode
  N21: IC1.pin38, LED6.cathode
  N22: IC1.pin39, LED5.cathode
  N23: IC1.pin40, LED4.cathode
  N24: Q1.B, R2.Pin_1, R3.Pin_1
  N25: Q1.C, LED1.anode, LED4.anode, LED5.anode, LED6.anode, LED7.anode, LED8.anode, LED9.anode, LED10.anode, LED11.anode, LED12.anode, LED13.anode, LED14.anode, LED15.anode, LED16.anode, LED17.anode
  N26: R4.Pin_1, Q2.B, R5.Pin_1
  N27: Q2.C, LED2.anode
  N28: Q3.B, R6.Pin_1, R7.Pin_1
  N29: Q3.C, LED3.anode
